# Fritzing sketch graficar (saved by Fritzing 0.9.3b)
breadboards: 1

parts:
  R2 = Trimmer Potentiometer [maximum_resistance=10kΩ package=THT]
  Q1 = NPN-Transistor [package="TO92 [THT]"]
  R3 = Resistor [tolerance=±5% resistance=15k package=THT]
  R4 = Photocell (LDR) [package=THT]
  LED1 = LED - 5mm [color="Red (633nm)" package="5 mm [THT]"]
  R5 = Resistor [tolerance=±5% resistance=220 package=THT]
  VCC1 = Battery block 9V

nets:
  N1: R2.leg1, R4.pin_1
  N2: R2.leg2, Q1.E
  N3: Q1.B, R3.Pin_0
  N4: Q1.C, LED1.cathode
  N5: R3.Pin_1, R5.Pin_1, VCC1.+
  N6: R4.pin_0, VCC1.-
  N7: LED1.anode, R5.Pin_0
