# Fritzing sketch prueba (saved by Fritzing 0.9.1b)
breadboards: 1

parts:
  VCC1 = Battery block 9V
  R1 = Resistor [tolerance=±5% resistance=220 package=THT]
  R2 = Resistor [tolerance=±5% resistance=100k package=THT]
  R3 = Trimmer Potentiometer [maximum_resistance=10kΩ package=THT]
  Q1 = PNP-Transistor [package="TO92 [THT]"]
  R4 = Photocell (LDR) [package=THT]
  LED1 = LED - 5mm [color="Red (633nm)" package="5 mm [THT]"]
  LED2 = LED - 5mm [color="Red (633nm)" package="5 mm [THT]"]

nets:
  N1: VCC1.-, R1.Pin_0, R2.Pin_0
  N2: R1.Pin_1, LED1.cathode, LED2.cathode
  N3: R2.Pin_1, R3.leg1, Q1.E
  N4: R3.wiper, Q1.B, R4.pin_0
  N5: R3.leg2, Q1.C, LED2.anode
