# Fritzing sketch Matriz 8x8 (saved by Fritzing 1.0.2b)
breadboards: 1

parts:
  Disp1 = 38mm 8x8 dot matrix row cathode led display with narrow pcb pads
  Componente1 = Arduino Uno (Rev3) - ICSP
  R1 = Resistor [tolerance=±5% power=0.25W resistance=330 package=THT]
  R2 = Resistor [tolerance=±5% power=0.25W resistance=330 package=THT]
  R3 = Resistor [tolerance=±5% power=0.25W resistance=330 package=THT]
  R4 = Resistor [tolerance=±5% power=0.25W resistance=330 package=THT]
  R5 = Resistor [tolerance=±5% power=0.25W resistance=330 package=THT]
  R6 = Resistor [tolerance=±5% power=0.25W resistance=330 package=THT]
  R7 = Resistor [tolerance=±5% power=0.25W resistance=330 package=THT]
  R8 = Resistor [tolerance=±5% power=0.25W resistance=330 package=THT]

nets:
  N1: Disp1.pin_1, R4.Pin_0
  N2: Disp1.pin_2, R5.Pin_1
  N3: Disp1.pin_3, Componente1.D10_PWM/SS
  N4: Disp1.pin_4, Componente1.D11_PWM/MOSI
  N5: Disp1.pin_5, R6.Pin_1
  N6: Disp1.pin_6, Componente1.D13/SCK
  N7: Disp1.pin_7, R7.Pin_1
  N8: Disp1.pin_8, R8.Pin_1
  N9: Disp1.pin_9, R1.Pin_0
  N10: Disp1.pin_10, Componente1.D6_PWM
  N11: Disp1.pin_11, Componente1.D5_PWM
  N12: Disp1.pin_12, R3.Pin_0
  N13: Disp1.pin_13, Componente1.D3_PWM
  N14: Disp1.pin_14, R2.Pin_0
  N15: Disp1.pin_15, Componente1.D1/TX
  N16: Disp1.pin_16, Componente1.D0/RX
  N17: Componente1.A0, R7.Pin_0
  N18: Componente1.A1, R8.Pin_0
  N19: Componente1.D8, R4.Pin_1
  N20: Componente1.D9_PWM, R5.Pin_0
  N21: Componente1.D12/MISO, R6.Pin_0
  N22: Componente1.D2, R2.Pin_1
  N23: Componente1.D4, R3.Pin_1
  N24: Componente1.D7, R1.Pin_1

// code stored in the sketch: matriz 8x8.ino
// Definición de pines para las columnas
const int colPins[8] = {0, 1, 3, 10, 11, 6, 13, 5};
// Definición de pines para las filas
const int rowPins[8] = {7, 2, 4, 8, A0, 9, A1, 12};

void setup() {
  // Configuramos los pines de las columnas como salidas
  for (int i = 0; i < 8; i++) {
    pinMode(colPins[i], OUTPUT);
    digitalWrite(colPins[i], HIGH); // Apagamos todas las columnas
  }

  // Configuramos los pines de las filas como salidas
  for (int i = 0; i < 8; i++) {
    pinMode(rowPins[i], OUTPUT);
    digitalWrite(rowPins[i], LOW); // Apagamos todas las filas
  }
}

void loop() {
  // Encendemos cada LED uno por uno
  for (int row = 0; row < 8; row++) {
    for (int col = 0; col < 8; col++) {
      lightLed(row, col);
      delay(100); // Esperamos 100 milisegundos
      clearLed(row, col);
    }
  }
}

// Función para encender un LED específico
void lightLed(int row, int col) {
  digitalWrite(colPins[col], LOW);  // Encendemos la columna
  digitalWrite(rowPins[row], HIGH); // Encendemos la fila
}

// Función para apagar un LED específico
void clearLed(int row, int col) {
  digitalWrite(colPins[col], HIGH); // Apagamos la columna
  digitalWrite(rowPins[row], LOW);  // Apagamos la fila
}
