# Fritzing sketch Dht11 y 22 (saved by Fritzing 1.0.2b)
breadboards: 1

parts:
  DHT1 = DHT11 Humitidy and Temperature Sensor
  Componente1 = Arduino Uno (Rev3)

nets:
  VDD: DHT1.VDD, Componente1.5V
  N1: DHT1.DATA, Componente1.D2
  GND: DHT1.GND, Componente1.GND

custom parts:
  DHT11 Humitidy and Temperature Sensor: DHT11 Humidity and Temperature Sensor
