# Fritzing sketch snake (saved by Fritzing 0.9.3b)
breadboards: 1

parts:
  Componente1 = Arduino Nano (Rev3.0)
  R1 = Rotary Potentiometer (Small) [maximum_resistance=100kΩ package=THT]  # not connected
  Componente2 = Thumb Joystick  # not connected
  Componente3 = LED Matrix - Serial Interface - Red/Green/Blue

nets:
  N1: Componente1.D10, Componente3.SCK
